# Fritzing sketch diagram (saved by Fritzing 0.9.4)

parts:
  SPKR1 = Loudspeaker
  J1 = Basic Servo
  Part2 = Arduino Uno (Rev3)
  HC-SR04_Sensor_1 = HC-SR04 Ultrasonic Distance Sensor

nets:
  N1: SPKR1.pin1, Part2.D3_PWM
  VCC: SPKR1.pin2, J1.vcc, Part2.5V, HC-SR04_Sensor_1.VCC
  GND: J1.gnd, Part2.GND, HC-SR04_Sensor_1.GND
  N2: J1.pulse, Part2.D2
  N3: Part2.D4, HC-SR04_Sensor_1.ECHO
  N4: Part2.D5_PWM, HC-SR04_Sensor_1.TRIG
